# Fritzing sketch 1 Button 1 LED (saved by Fritzing 0.9.3b)
breadboards: 1

parts:
  Part1 = Arduino Uno (Rev3)
  LED1 = LED - 5mm [color="Red (633nm)" package="5 mm [THT]"]
  R1 = Resistor [tolerance=±5% resistance=220 package=THT]
  S1 = Pushbutton [package="[THT]"]
  R2 = Resistor [tolerance=±5% resistance=10k package=THT]  # not connected

nets:
  N1: Part1.D2, LED1.anode
  N2: Part1.D4, S1.Pin_3, S1.Pin_4
  N3: Part1.GND, R1.Pin_1
  N4: LED1.cathode, R1.Pin_0
  N5: S1.Pin_1, S1.Pin_2
